// Logisim project 8Bit_CPU.circ as structural Verilog: 2 circuits, main circuit main
module main (
);

  wire and_1_out, Clock_out;
  wire [7:0] undriven;

  LED led_1 (.in(Clock_out));
  Clock Clock (.out(Clock_out));
  LED led_2 (.in(and_1_out));
  buf and_1 (and_1_out, Clock_out);  // AND_Gate AND_Gate
  LED led_3 (.in(undriven[5]));
  LED led_4 (.in(undriven[4]));
  LED led_5 (.in(undriven[7]));
  LED led_6 (.in(undriven[6]));
  LED led_7 (.in(undriven[0]));
  LED led_8 (.in(undriven[1]));
  LED led_9 (.in(undriven[2]));
  LED led_10 (.in(undriven[3]));
endmodule

module SR_latch (
  input  in_1,
  input  in_2,
  output out_3,
  output out_4
);

  nor nor_1 (out_3, in_1, out_4);
  nor nor_2 (out_4, out_3, in_2);
endmodule
